# Fritzing sketch circuit-diagram (saved by Fritzing 0.9.3b)
breadboards: 1

parts:
  Part1 = Espruino
  Part2 = Soil Moisture Sensor
  DS1 = DS18B20 1-Wire Temperature Sensor [part_number=DS18B20]
  R1 = Resistor [tolerance=±10% resistance=4.7k package="1206 [SMD]"]

nets:
  N1: Part1.A0, R1.Pin_1
  N2: Part1.A1, Part2.SIG
  VCC: Part1.3.3, Part2.VCC, DS1.VDD, R1.Pin_0
  GND: Part1.GND, Part2.GND, DS1.GND

notes:
  Operational Gude:
  ==============
  LED1 - Green - Signals temp OK
  LED2 - Red - Signals temp outwith range
  LED3 - Blue - Signals low moisture

custom parts:
  Espruino: Espruino is an Interactive JavaScript interpreter for Microcontrollers, so you can program them quickly and easily. The Espruino Board on KickStarter is a specially designed computer with Espruino software pre-installed. It complements the Espruino software with masses of functionality and great battery life.
